# Fritzing sketch Cicuit (saved by Fritzing 0.9.3b)
breadboards: 1

parts:
  Part1 = Arduino Uno (Rev3)
  LCD1 = LCD screen
  R1 = Rotary Potentiometer (Small) [maximum_resistance=100kΩ package=THT]
  Part2 = FC-28 Soil Hygrometer Module - Probe
  Part3 = FC-28 Soil Hygrometer Module
  Part4 = 4x4 Keypad [part_number=101207]
  DHT11_1 = DHT11 module
  e-radionica_com1 = LM393 LDR breakout [part_number=100027]
  U1 = RELAY [package=relay-jzc]

nets:
  N1: Part1.A0, Part3.AO
  N2: Part1.A1, e-radionica_com1.AO
  N3: Part1.A2, Part4.4
  N4: Part1.A3, Part4.3
  N5: Part1.A4/SDA, Part4.2
  N6: Part1.A5/SCL, Part4.1
  N7: Part1.D8, Part4.5
  N8: Part1.D9_PWM, Part4.6
  N9: Part1.D10_PWM/SS, Part4.7
  N10: Part1.D11_PWM/MOSI, LCD1.E
  N11: Part1.D12/MISO, LCD1.RS
  N12: Part1.D13/SCK, Part4.8
  N13: Part1.D2, LCD1.DB7
  N14: Part1.D3_PWM, LCD1.DB6
  N15: Part1.D4, LCD1.DB5
  N16: Part1.D5_PWM, LCD1.DB4
  N17: Part1.D6_PWM, U1.NO
  N18: Part1.D7, DHT11_1.DATA
  N19: Part1.3V3, LCD1.LED+
  VCC: Part1.5V, LCD1.VDD, R1.leg2, Part3.VCC, DHT11_1.VCC, e-radionica_com1.VCC, U1.COIL2
  GND: Part1.GND, LCD1.VSS, LCD1.R/W, LCD1.LED-, R1.leg1, Part3.GND, DHT11_1.GND, e-radionica_com1.GND, U1.NC
  N20: LCD1.V0, R1.wiper
  N21: Part2.POS, Part3.NEG
  N22: Part2.NEG, Part3.POS

custom parts:
  FC-28 Soil Hygrometer Module - Probe: The FC-28 is a soil hygrometer module that uses the Texas Instruments LM393 comparator chip to provide an analog measurement of soil humidity.
  FC-28 Soil Hygrometer Module: The FC-28 is a soil hygrometer module that uses the Texas Instruments LM393 comparator chip to provide an analog measurement of soil humidity. The digital output is high when soil moisture is over a certain threshold, as determined by adjusting the potentiometer.
  4x4 Keypad: Matrix membrane keypad 4x4
  DHT11 module: DHT11 black pcb module
